# Fritzing sketch rollo (saved by Fritzing 0.9.9b)
circuit board: 8.46667cm x 5.64444cm
breadboards: 1

parts:
  U2 = FS1000A - 433Mhz RF Transmitter [package=THT]
  VCC1 = Battery
  R1 = Resistor [tolerance=±5% power=0.25 resistance=2.2k package=THT]
  R2 = Resistor [tolerance=±5% power=0.25 resistance=10000 package=THT]
  S1 = Pushbutton [package="[THT]"]
  U3 = ESP8266 WiFi Module [part_number=ESP8266]

nets (from the schematic view):
  N1: U2.DATA, U3.GPIO_4
  VCC: U2.VCC, VCC1.+, S1.Pin_1, S1.Pin_2, U3.VCC, U3.CH_PD
  GND: U2.GND, VCC1.-, R1.Pin_1, R2.Pin_0, U3.GND
  N2: R1.Pin_0, U3.GPIO_15
  N3: R2.Pin_1, S1.Pin_3, S1.Pin_4, U3.GPIO_5

notes:
  GND
  IO5 = Button
  EN
  IO15 (2,2k-GND)
  3V3
  IO4 = Sender
  Antenne 17cm

custom parts:
  FS1000A - 433Mhz RF Transmitter: This is 433Mhz RF transmitter with receiver kit for Arduino ARM MCU wireless Application environment: Remote control switch, receiver module, motorcycles, automobile anti-theft products, home security products, electric doors, shutter doors, windows, remote control socket, remote control LED, remote audio remote control electric doors, garage door remote control, remote control retractable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
